# Fritzing sketch circuitoMain (saved by Fritzing 0.9.3b)
circuit board: 24.5417cm x 17.272cm
breadboards: 12

parts:
  U1 = 74HC595 [package="DIP16 [THT]"]
  U2 = 74HC595 [package="DIP16 [THT]"]
  U3 = 74HC595 [package="DIP16 [THT]"]
  U4 = 74HC595 [package="DIP16 [THT]"]
  U5 = 74HC595 [package="DIP16 [THT]"]
  U6 = 74HC595 [package="DIP16 [THT]"]
  U8 = 74HC595 [package="DIP16 [THT]"]
  Q74 = NPN-Transistor [package="TO92 [THT]"]
  Q75 = NPN-Transistor [package="TO92 [THT]"]
  Q76 = NPN-Transistor [package="TO92 [THT]"]
  Q77_OPA = NPN-Transistor [package="TO92 [THT]"]
  Q78 = NPN-Transistor [package="TO92 [THT]"]
  Q79 = NPN-Transistor [package="TO92 [THT]"]
  Q80 = NPN-Transistor [package="TO92 [THT]"]
  Q81 = NPN-Transistor [package="TO92 [THT]"]
  Q83 = NPN-Transistor [package="TO92 [THT]"]
  Q95 = NPN-Transistor [package="TO92 [THT]"]
  Q97 = NPN-Transistor [package="TO92 [THT]"]
  Q98 = NPN-Transistor [package="TO92 [THT]"]
  Q103 = NPN-Transistor [package="TO92 [THT]"]
  Q107 = NPN-Transistor [package="TO92 [THT]"]
  Q109 = NPN-Transistor [package="TO92 [THT]"]
  Q110 = NPN-Transistor [package="TO92 [THT]"]
  Q111 = NPN-Transistor [package="TO92 [THT]"]
  Q112 = NPN-Transistor [package="TO92 [THT]"]
  Q113 = NPN-Transistor [package="TO92 [THT]"]
  Q115 = NPN-Transistor [package="TO92 [THT]"]
  Q116 = NPN-Transistor [package="TO92 [THT]"]
  Q119 = NPN-Transistor [package="TO92 [THT]"]
  Q124 = NPN-Transistor [package="TO92 [THT]"]
  Q125 = NPN-Transistor [package="TO92 [THT]"]
  Q126 = NPN-Transistor [package="TO92 [THT]"]
  Q128 = NPN-Transistor [package="TO92 [THT]"]
  Q129 = NPN-Transistor [package="TO92 [THT]"]
  Q131 = NPN-Transistor [package="TO92 [THT]"]
  Q133 = NPN-Transistor [package="TO92 [THT]"]
  Q134 = NPN-Transistor [package="TO92 [THT]"]
  Q139 = NPN-Transistor [package="TO92 [THT]"]
  Q140 = NPN-Transistor [package="TO92 [THT]"]
  Q141 = NPN-Transistor [package="TO92 [THT]"]
  Q142 = NPN-Transistor [package="TO92 [THT]"]
  Q143 = NPN-Transistor [package="TO92 [THT]"]
  Q144 = NPN-Transistor [package="TO92 [THT]"]
  Q145 = NPN-Transistor [package="TO92 [THT]"]
  Q146 = NPN-Transistor [package="TO92 [THT]"]
  Q147 = NPN-Transistor [package="TO92 [THT]"]
  Q148 = NPN-Transistor [package="TO92 [THT]"]
  Q149 = NPN-Transistor [package="TO92 [THT]"]
  Q150 = NPN-Transistor [package="TO92 [THT]"]
  Q151 = NPN-Transistor [package="TO92 [THT]"]
  Q152 = NPN-Transistor [package="TO92 [THT]"]
  Q153 = NPN-Transistor [package="TO92 [THT]"]
  Q154 = NPN-Transistor [package="TO92 [THT]"]
  Q155 = NPN-Transistor [package="TO92 [THT]"]
  Q156 = NPN-Transistor [package="TO92 [THT]"]
  Q157 = NPN-Transistor [package="TO92 [THT]"]
  Q158 = NPN-Transistor [package="TO92 [THT]"]
  Q159 = NPN-Transistor [package="TO92 [THT]"]
  Q160 = NPN-Transistor [package="TO92 [THT]"]
  Q161 = NPN-Transistor [package="TO92 [THT]"]
  Q162 = NPN-Transistor [package="TO92 [THT]"]
  Q163 = NPN-Transistor [package="TO92 [THT]"]
  Q164 = NPN-Transistor [package="TO92 [THT]"]
  Raspberry_Pi_1 = Raspberry Pi 3 [part_number=RPI-3-V1.2]

nets:
  N1: U1.Q1, U1.Q4, U1.OE, Q133.E
  N2: U1.Q2, Q134.E
  N3: U1.Q3, U1.DS, U2.Q7, Q80.E
  N4: U1.Q5, Q139.E
  N5: U1.Q6, U1.SH_CP, Q113.E
  N6: U1.Q7, U2.SH_CP, U3.SH_CP, U4.SH_CP, U5.Q7, U6.SH_CP, U8.Q7, Raspberry_Pi_1.GPIO6
  GND: U1.GND, U2.GND, U2.OE, U3.OE, U4.OE, U5.GND, U6.GND, U6.OE, U8.GND, Q74.C, Q75.C, Q76.C, Q77_OPA.C, Q78.C, Q79.C, Q80.C, Q81.C, Q83.C, Q95.C, Q97.C, Q103.C, Q107.C, Q109.C, Q110.C, Q111.C, Q112.C, Q113.C, Q115.C, Q116.C, Q119.C, Q125.C, Q126.C, Q129.C, Q131.C, Q133.C, Q134.C, Q140.C, Q141.C, Q142.C, Q143.C, Q144.C, Q145.C, Q146.C, Q147.C, Q148.C, Q149.C, Q150.C, Q151.C, Q152.C, Q153.C, Q154.C, Q155.C, Q157.C, Q158.C, Q159.C, Q160.C, Q161.C, Q162.C, Q163.C, Q164.C, Raspberry_Pi_1.GND
  N7: U1.Q7', U2.DS
  N8: U1.MR, Q79.E
  N9: U2.Q1, Q144.E
  N10: U2.Q2, Q142.E
  N11: U2.Q3, Q143.E
  N12: U2.Q4, Q131.E
  N13: U2.Q5, Q119.E
  N14: U2.Q6, Q98.E
  N15: U2.Q7', U3.DS
  VCC: U2.MR, U2.VCC, U3.MR, U3.VCC, U4.MR, U4.VCC, U6.MR, U6.VCC, Raspberry_Pi_1.3v3
  N16: U2.ST_CP, U3.ST_CP, U4.ST_CP, U6.ST_CP, Raspberry_Pi_1.GPIO5
  N17: U2.Q0, Q141.E
  N18: U3.Q1, Q145.E
  N19: U3.Q2, Q146.E
  N20: U3.Q3, Q147.E
  N21: U3.Q4, Q124.E
  N22: U3.Q5, Q116.E
  N23: U3.Q6, Q95.E
  N24: U3.Q7, Q81.E
  N25: U3.Q0, Q148.E
  N26: U4.Q1, Q157.E
  N27: U4.Q2, Q158.E
  N28: U4.Q3, Q159.E
  N29: U4.Q4, Q129.E
  N30: U4.Q5, Q107.E
  N31: U4.Q7, Q76.E
  N32: U4.DS, U6.Q7'
  N33: U4.Q0, Q160.E
  N34: U5.Q3, U5.DS, U6.Q7, Q75.E
  N35: U5.Q4, U5.Q5, U5.OE, Q150.E, Q152.E
  N36: U5.Q6, U5.SH_CP, Q128.E
  N37: U5.Q7', U6.DS
  N38: U5.MR, Q77_OPA.E
  N39: U6.Q1, Q154.E
  N40: U6.Q2, Q156.E
  N41: U6.Q3, Q155.E
  N42: U6.Q4, Q125.E
  N43: U6.Q5, Q111.E
  N44: U6.Q0, Q153.E
  N45: U8.Q3, U8.DS
  N46: U8.Q4, U8.OE, Q161.E
  N47: U8.Q5, Q164.E
  N48: U8.Q6, U8.SH_CP, Q126.E
  N49: U8.MR, Q74.E
